# Fritzing sketch ODroid600_friting_diagram (saved by Fritzing 0.9.10b)
breadboards: 1

parts:
  Part1 = Arduino Uno (Rev3)
  CONN1 = USB connector [package=THT]  # not connected
  microSD1 = MicroSD Card Module  # not connected
  LED6 = LED - 3mm [color="Orange (605nm)" current=0.030 package="3 mm [THT]"]
  LED7 = LED - 3mm [color="Orange (605nm)" current=0.030 package="3 mm [THT]"]
  Q2 = LTR-301 [package=ltr-301]
  Q3 = LTR-301 [package=ltr-301]
  LED9 = LED - 3mm [color="Orange (605nm)" current=0.030 package="3 mm [THT]"]
  Q4 = LTR-301 [package=ltr-301]
  Q5 = LTR-301 [package=ltr-301]
  R1 = Resistor [tolerance=±5% resistance=1k package="2512 [SMD]"]
  R2 = Resistor [tolerance=±5% resistance=1k package="2512 [SMD]"]
  R3 = Resistor [tolerance=±5% resistance=1k package="2512 [SMD]"]
  R4 = Resistor [tolerance=±5% resistance=1k package="2512 [SMD]"]
  LED8 = LED - 3mm [color="Orange (605nm)" current=0.030 package="3 mm [THT]"]
  R5 = Resistor [tolerance=±5% resistance=1k package="2512 [SMD]"]
  R6 = Resistor [tolerance=±5% resistance=1k package="2512 [SMD]"]
  R7 = Resistor [tolerance=±5% resistance=1k package="2512 [SMD]"]
  R8 = Resistor [tolerance=±5% resistance=1k package="2512 [SMD]"]

nets:
  N1: Part1.A0, Q4.C, R7.Pin_1
  N2: Part1.A1, Q5.C, R6.Pin_1
  N3: Part1.A2, Q2.E, Q3.C, Q3.E, Q4.E, Q5.E, R5.Pin_1
  N4: Part1.A3, Q2.C, R8.Pin_1
  N5: Part1.D2, R1.Pin_0
  N6: Part1.D3_PWM, R2.Pin_0
  N7: Part1.D4, R3.Pin_0
  N8: Part1.D5_PWM, R4.Pin_0
  N9: LED6.cathode, LED7.cathode, LED9.cathode, LED8.cathode
  N10: LED6.anode, R1.Pin_1
  N11: LED7.anode, R2.Pin_1
  N12: LED9.anode, R3.Pin_1
  N13: R4.Pin_1, LED8.anode
  N14: R5.Pin_0, R6.Pin_0, R7.Pin_0, R8.Pin_0
